# Fritzing sketch Circuito_Modulo_Bomba_Definitivo (saved by Fritzing 0.9.3b)
breadboards: 1

parts:
  Sensor_de_Nível_de_água = Water Level Sensor
  U1 = NodeMCU V1.0
  Componente2 = Logic Level Converter
  Display1 = LCD screen 16x2 IIC [part_number=101290]
  Motor_Bomba = mystery part, 3 pins [chip_label=Bomba]
  Relé_5V = KY-019 5V Relay Module [package="Breakout board"]

nets:
  N1: Sensor_de_Nível_de_água.SIG, Componente2.TX_HV
  VCC: Sensor_de_Nível_de_água.VCC, U1.Vin, Componente2.HV, Display1.VCC, Relé_5V.+
  GND: Sensor_de_Nível_de_água.GND, U1.GND, Componente2.GND, Display1.GND, Relé_5V.-
  N2: U1.D1, Display1.SCL
  N3: U1.D2, Display1.SDA
  N4: U1.3V3, Componente2.LV
  N5: U1.D8, Relé_5V.S
  N6: U1.A0, Componente2.TX_LV
  N7: Motor_Bomba.pin2, Relé_5V.Common
  N8: Motor_Bomba.pin3, Relé_5V.NO

custom parts:
  Water Level Sensor: A water level sensor. This sensor operates at 3V to 5V. The Sig (signal) pin outputs an analogue signal that is in proportion to the amount of water in contact with the sensor.
  NodeMCU V1.0: ESP8266 based NodeMCU
  LCD screen 16x2 IIC: LCD screen with HD44780 controller enables showing text, symbols, value or anything else that comes from Croduino/Arduino. It is capable of showing 16 symbols in two lines and therefore can be used in many projects that need to send clearly visible and legible output information.. • Color of symbols: White • Backlight: Blue • Dimensions: 80 x 36 x 12 mm • Screen dimensions: 64.5 x 16 mm •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
  KY-019 5V Relay Module: KY-019 5V Relay module, used to control AC circuits.
