# Fritzing sketch Circuito_Modulo_Irrigacao_Definitivo (saved by Fritzing 0.9.3b)
breadboards: 1

parts:
  Válvula_Solenoide = Plastic Solenoid Valve
  Relé_5V = KY-019 5V Relay Module [package="Breakout board"]
  Display1 = LCD screen 16x2 IIC [part_number=101290]
  Sensor_de_Umidade_de_Solo_(Pontas) = FC-28 Soil Hygrometer Module - Probe
  Sensor_de_Umidade_de_solo_(Amplificador) = FC-28 Soil Hygrometer Module
  U1 = NodeMCU V1.0

nets:
  N1: Válvula_Solenoide.no_name_yet#1, Relé_5V.Common
  N2: Válvula_Solenoide.no_name_yet#2, Relé_5V.NO
  N3: Relé_5V.S, U1.D7
  VCC: Relé_5V.+, Display1.VCC, Sensor_de_Umidade_de_solo_(Amplificador).VCC, U1.Vin
  GND: Relé_5V.-, Display1.GND, Sensor_de_Umidade_de_solo_(Amplificador).GND, U1.GND
  N4: Display1.SDA, U1.D2
  N5: Display1.SCL, U1.D1
  N6: Sensor_de_Umidade_de_Solo_(Pontas).POS, Sensor_de_Umidade_de_solo_(Amplificador).POS
  N7: Sensor_de_Umidade_de_Solo_(Pontas).NEG, Sensor_de_Umidade_de_solo_(Amplificador).NEG
  N8: Sensor_de_Umidade_de_solo_(Amplificador).AO, U1.A0

custom parts:
  KY-019 5V Relay Module: KY-019 5V Relay module, used to control AC circuits.
  LCD screen 16x2 IIC: LCD screen with HD44780 controller enables showing text, symbols, value or anything else that comes from Croduino/Arduino. It is capable of showing 16 symbols in two lines and therefore can be used in many projects that need to send clearly visible and legible output information.. • Color of symbols: White • Backlight: Blue • Dimensions: 80 x 36 x 12 mm • Screen dimensions: 64.5 x 16 mm •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
  FC-28 Soil Hygrometer Module - Probe: The FC-28 is a soil hygrometer module that uses the Texas Instruments LM393 comparator chip to provide an analog measurement of soil humidity.
  FC-28 Soil Hygrometer Module: The FC-28 is a soil hygrometer module that uses the Texas Instruments LM393 comparator chip to provide an analog measurement of soil humidity. The digital output is high when soil moisture is over a certain threshold, as determined by adjusting the potentiometer.
  NodeMCU V1.0: ESP8266 based NodeMCU
