# Fritzing sketch Diagrama_ModuloBomba_Arduino (saved by Fritzing 0.9.3b)
breadboards: 1

parts:
  BC547 = NPN-Transistor [package="TO92 [THT]"]
  R1 = Resistor [tolerance=±5% resistance=330 package=THT]
  Arduino = Arduino Uno (Rev3)
  Reservatório/Poço = mystery part, 2 pins [chip_label=Reservatório/Poço]
  R2 = Resistor [tolerance=±5% resistance=220 package=THT]
  LED1 = LED - 5mm [color="Red (633nm)" package="5 mm [THT]"]

nets:
  N1: BC547.E, R1.Pin_1, Arduino.D2, Reservatório/Poço.pin1
  N2: BC547.B, Reservatório/Poço.pin2
  N3: BC547.C, Arduino.GND, R2.Pin_0
  N4: R1.Pin_0, Arduino.5V
  N5: Arduino.D4, LED1.anode
  N6: R2.Pin_1, LED1.cathode
