# Fritzing sketch Modulo_Bomba (saved by Fritzing 0.9.3b)
breadboards: 1

parts:
  R1 = Resistor [tolerance=±5% resistance=330 package=THT]
  Componente1 = Arduino Uno (Rev3)
  Q1 = NPN-Transistor [package="TO92 [THT]"]
  U1 = mystery part, 3 pins [chip_label=?]
  LED1 = LED - 5mm [color="Red (633nm)" package="5 mm [THT]"]
  R2 = Resistor [tolerance=±5% resistance=220 package=THT]

nets:
  N1: R1.Pin_0, Componente1.D7, Q1.E, U1.pin3
  N2: R1.Pin_1, Componente1.5V
  N3: Componente1.D5_PWM, LED1.cathode
  N4: Componente1.GND, Q1.C, R2.Pin_1
  N5: Q1.B, U1.pin2
  N6: LED1.anode, R2.Pin_0
