# Fritzing sketch Modulo_Bomba_NodeMCU2 (saved by Fritzing 0.9.3b)
breadboards: 1

parts:
  WeMos_D1_(ESP-12E) = WeMos D1 Mini
  BC547 = NPN-Transistor [package="TO92 [THT]"]
  R1 = Resistor [tolerance=±5% resistance=220 package=THT]
  LED1 = LED - 5mm [color="Red (633nm)" package="5 mm [THT]"]
  Reservatório/Poço = mystery part, 2 pins [chip_label=Reservatório]

nets:
  N1: WeMos_D1_(ESP-12E).D3, BC547.E, Reservatório/Poço.pin1
  N2: WeMos_D1_(ESP-12E).D6, LED1.cathode
  N3: WeMos_D1_(ESP-12E).G, BC547.C
  N4: BC547.B, Reservatório/Poço.pin2
  N5: R1.Pin_1, LED1.anode
